// Logisim project projetopentregar.circ as structural Verilog: 8 circuits, main circuit main
module main (
  input  RST
);

  wire ALUSrc, Branch, CLK, Jump, MemRead, MemToRead, MemWrite, RegWrite;
  wire [2:0] ALUOp, funct, OffSel, rd, rs1, rs2;
  wire [3:0] opcode;
  wire [5:0] B_offset, I_imm, S_offset;
  wire [7:0] intructionf_1_currentpc, NextPC, PC2;
  wire [8:0] J_offset;
  wire [15:0] ALU_Data, BRData, data, DataOut, instrucao, Offset_Imm, rd1, rd2;

  Clock u_CLK (.out(CLK));
  Multiplexer #(.width(16)) multiplexer_1 (.in0(Offset_Imm), .in1(rd2), .out(ALU_Data));  // open: sel
  IntructionF intructionf_1 (
    .CLK(CLK), .RST(RST), .NextPC(NextPC), .CurrentPC(intructionf_1_currentpc), .Instrucao(instrucao));
  Adder adder_1 (.a(8'h2), .b(intructionf_1_currentpc), .out(PC2));  // open: cin, cout
  // Probe on instrucao
  Multiplexer #(.width(16)) multiplexer_2 (.in0(data), .in1(DataOut), .out(BRData), .sel(MemToRead));
  InstuctionD instuctiond_1 (
    .Instrucao(instrucao), .funct(funct), .rs2(rs2), .rs1(rs1), .rd(rd), .opcode(opcode), .I_imm(I_imm),
    .S_offset(S_offset), .B_offset(B_offset), .J_offset(J_offset));
  UC uc_1 (
    .opcode(opcode), .funct(funct), .CLK(CLK), .RegWrite(RegWrite), .ALUSrc(ALUSrc), .Branch(Branch),
    .MemWrite(MemWrite), .Jump(Jump), .MemRead(MemRead), .MemToRead(MemToRead), .ALUControl(ALUOp));  // open: ALUOp
  // Probe on rd1
  BR br_1 (
    .CLK(CLK), .RST(RST), .RegWrite(RegWrite), .RS1(rs1), .RS2(rs2), .RD(rd), .Data(BRData), .rd1(rd1),
    .rd2(rd2));
  // Probe on rd2
  ImmGen immgen_1 (
    .OffSel(OffSel), .I_Imm(I_imm), .S_Offset(S_offset), .B_Offset(B_offset), .J_Offset(J_offset),
    .Offset_Imm(Offset_Imm));
  // Probe on rd1
  DM dm_1 (.Address(data), .WriteEnable(RegWrite), .MemRead(MemRead), .CLK(CLK), .WriteData(rd2), .DataOut(DataOut));
  ULA ula_1 (.src1(rd1), .src2(ALU_Data), .ALUOperation(ALUOp), .Result(data));

  // Notes on the sheet:
  //   2° Entrada da ULA
  //   WriteBack BR
endmodule

module IntructionF (
  input  CLK,
  input  RST,
  input  [7:0] NextPC,
  output [7:0] CurrentPC,
  output [15:0] Instrucao
);

  Register PC (.D(NextPC), .en(1'b1), .clk(CLK), .Q(CurrentPC), .clr(RST));
  // ROM #(.line("dual")) rom_1: pin names not known; wires that end beside it: CurrentPC

  // Notes on the sheet:
  //   contents of rom_1 (hex, n*v repeats v):
  //   2 98
  //   Memoria de instrucoes
endmodule

module InstuctionD (
  input  [15:0] Instrucao,
  output [2:0] funct,
  output [2:0] rs2,
  output [2:0] rs1,
  output [2:0] rd,
  output [3:0] opcode,
  output [5:0] I_imm,
  output [5:0] S_offset,
  output [5:0] B_offset,
  output [8:0] J_offset
);


  assign B_offset = Instrucao[5:0];
  assign funct = Instrucao[2:0];
  assign I_imm = Instrucao[5:0];
  assign J_offset = Instrucao[8:0];
  assign opcode = Instrucao[15:12];
  assign rd = Instrucao[11:9];
  assign rs1 = Instrucao[8:6];
  assign rs2 = Instrucao[5:3];
  assign S_offset = Instrucao[5:0];

  // Notes on the sheet:
  //   Imetiato Tipo I
  //   Offset Tipo B
  //   Offset Tipo S
  //   Offset Tipo J
endmodule

module BR (
  input  CLK,
  input  RST,
  input  RegWrite,
  input  [2:0] RS1,
  input  [2:0] RS2,
  input  [2:0] RD,
  input  [15:0] Data,
  output [15:0] rd1,
  output [15:0] rd2
);

  wire WE_R1, WE_R2, WE_R3, WE_R4, WE_R5, WE_R6, WE_R7;
  wire [15:0] Q_R0, Q_R1, Q_R2, Q_R3, Q_R4, Q_R5, Q_R6, Q_R7;

  Demultiplexer #(.select(3)) demultiplexer_1 (
    .out1(WE_R1), .out2(WE_R2), .out3(WE_R3), .out4(WE_R4), .out5(WE_R5), .out6(WE_R6), .out7(WE_R7),
    .in(RegWrite), .sel(RD));  // open: out0
  Register #(.trigger("falling"), .width(16)) R0 (.D({16{1'b0}}), .clk(CLK), .Q(Q_R0), .clr(RST));  // open: en
  Register #(.trigger("falling"), .width(16)) R4 (.D(Data), .en(WE_R4), .clk(CLK), .Q(Q_R4), .clr(RST));
  Register #(.width(16)) R1 (.D(Data), .en(WE_R1), .clk(CLK), .Q(Q_R1), .clr(RST));
  Register #(.trigger("falling"), .width(16)) R5 (.D(Data), .en(WE_R5), .clk(CLK), .Q(Q_R5), .clr(RST));
  Register #(.trigger("falling"), .width(16)) R2 (.D(Data), .en(WE_R2), .clk(CLK), .Q(Q_R2), .clr(RST));
  Register #(.trigger("falling"), .width(16)) R6 (.D(Data), .en(WE_R6), .clk(CLK), .Q(Q_R6), .clr(RST));
  Register #(.trigger("falling"), .width(16)) R3 (.D(Data), .en(WE_R3), .clk(CLK), .Q(Q_R3), .clr(RST));
  Register #(.trigger("falling"), .width(16)) R7 (.D(Data), .en(WE_R7), .clk(CLK), .Q(Q_R7), .clr(RST));
  Multiplexer #(.select(3), .width(16)) multiplexer_1 (
    .in0(Q_R0), .in1(Q_R1), .in2(Q_R2), .in3(Q_R3), .in4(Q_R4), .in5(Q_R5), .in6(Q_R6), .in7(Q_R7),
    .out(rd1), .sel(RS1));
  Multiplexer #(.select(3), .width(16)) multiplexer_2 (
    .in0(Q_R0), .in1(Q_R1), .in2(Q_R2), .in3(Q_R3), .in4(Q_R4), .in5(Q_R5), .in6(Q_R6), .in7(Q_R7),
    .out(rd2), .sel(RS2));

  // Other names for the same wires on the sheet: RW = RegWrite
endmodule

module ULA (
  input  [15:0] src1,
  input  [15:0] src2,
  input  [2:0] ALUOperation,
  output [15:0] Result
);

  wire comparator_1_lt;
  wire [15:0] Add, And_Logic, Or_Logic, Slt_Logic, Sub;

  Adder #(.width(16)) adder_1 (.a(src1), .b(src2), .out(Add));  // open: cin, cout
  Subtractor #(.width(16)) subtractor_1 (.a(src1), .b(src2), .out(Sub));  // open: bin, bout
  assign And_Logic = src1 & src2;  // AND_Gate and_1, 16 bits wide
  assign Or_Logic = src1 | src2;  // OR_Gate or_1, 16 bits wide
  Comparator #(.width(16)) comparator_1 (.a(src1), .b(src2), .lt(comparator_1_lt));  // open: gt, eq
  assign Slt_Logic = {{15{1'b0}}, comparator_1_lt};  // Bit_Extender bit_extender_1
  Multiplexer #(.select(3), .width(16)) multiplexer_1 (
    .in0(Add), .in1(Sub), .in2(And_Logic), .in3(Or_Logic), .in4(Slt_Logic), .out(Result), .sel(ALUOperation));  // open: in5, in6, in7
  // Probe on Result

  // Other names for the same wires on the sheet: ALUOp[2:0] = ALUOperation

  // Notes on the sheet:
  //   Add
  //   Sub
  //   And
  //   Or
  //   Set Last Than
  //   ALUOp
  //   000 - Add (0)
  //   001 - Sub (1)
  //   010 - And (2)
  //   011 - Or (3)
  //   100 - Slt (4)
endmodule

module UC (
  input  [3:0] opcode,
  input  [2:0] funct,
  input  CLK,
  input  [2:0] ALUOp,
  output RegWrite,
  output ALUSrc,
  output Branch,
  output MemWrite,
  output Jump,
  output MemRead,
  output MemToRead,
  output [2:0] ALUControl
);

  wire alu0, Beq, I_AR, is_I, R_Type;
  wire [2:0] bit_extender_1_out, Type_R;

  or or_1 (alu0, Beq, Beq);
  Decoder #(.select(4)) decoder_1 (
    .out0(R_Type), .out1(I_AR), .out2(MemRead), .out3(MemWrite), .out4(Beq), .out5(Beq), .out6(Jump),
    .sel(opcode), .en(CLK));  // open: out7, out8, out9, out10, out11, out12, out13, out14, out15
  assign ALUControl = {Jump, {2{Beq}}} | Type_R;  // OR_Gate or_2, 3 bits wide
  assign bit_extender_1_out = {{2{1'b0}}, R_Type};  // Bit_Extender bit_extender_1
  assign Type_R = bit_extender_1_out & funct;  // AND_Gate and_1, 3 bits wide
  or or_3 (is_I, I_AR, MemRead);
  or or_4 (RegWrite, is_I, Jump, R_Type);
  or or_5 (ALUSrc, I_AR, MemRead, MemWrite);
  or or_6 (Branch, Beq, Beq);

  assign MemToRead = MemRead;

  // Other names for the same wires on the sheet: ALUCtrl[2:0] = ALUControl; I_Load = MemRead; Bne = Beq;
  //   SRC3[2:0] = {Jump, {2{Beq}}}; Jal = Jump; SW = MemWrite

  // Notes on the sheet:
  //   RegWrite
  //   ALUSrc
  //   Branch
endmodule

module DM (
  input  [15:0] Address,
  input  WriteEnable,
  input  MemRead,
  input  CLK,
  input  [15:0] WriteData,
  output [15:0] DataOut
);

  RAM #(.addrWidth(5), .dataWidth(16)) ram_1 (
    .addr(Address[4:0]), .we(WriteEnable), .oe(MemRead), .clk(CLK), .din(WriteData), .dout(DataOut));

  // Other names for the same wires on the sheet: ME = MemRead; WD[15:0] = WriteData; WE = WriteEnable
endmodule

module ImmGen (
  input  [2:0] OffSel,
  input  [5:0] I_Imm,
  input  [5:0] S_Offset,
  input  [5:0] B_Offset,
  input  [8:0] J_Offset,
  output [15:0] Offset_Imm
);

  wire [15:0] B_Offset16, Imm_16, J_Offset16, S_Offset16;

  assign B_Offset16 = {{10{B_Offset[5]}}, B_Offset};  // Bit_Extender bit_extender_1
  assign J_Offset16 = {{7{J_Offset[8]}}, J_Offset};  // Bit_Extender bit_extender_2
  assign Imm_16 = {{10{I_Imm[5]}}, I_Imm};  // Bit_Extender bit_extender_3
  assign S_Offset16 = {{10{S_Offset[5]}}, S_Offset};  // Bit_Extender bit_extender_4
  Multiplexer #(.select(3), .width(16)) multiplexer_1 (
    .in0(Imm_16), .in1(S_Offset16), .in2(B_Offset16), .in3(J_Offset16), .out(Offset_Imm), .sel(OffSel));  // open: in4, in5, in6, in7

  // Notes on the sheet:
  //   Instrucao tipo I
  //   Offset tipo S
  //   Offset tipo B
  //   Offset tipo J
endmodule
